// Logisim project FLEX_CPU.circ as structural Verilog
module main (
);

  wire and_1_out, button_1_out, button_2_out, clock_1_out, flex_6016_1_write_mem;
  wire [6:0] flex_6016_1_o0;
  wire [7:0] ram_1_data;
  wire [7:7] flex_6016_1_o7;
  wire [15:0] flex_6016_1_a0;

  Button button_1 (.out(button_1_out));
  Button button_2 (.out(button_2_out));
  Clock clock_1 (.out(clock_1_out));
  FLEX_6016 flex_6016_1 (
    .IRQ(button_1_out), .NMI(button_2_out), .CLOCK(clock_1_out), .I7(ram_1_data[7]), .I6(ram_1_data[6]),
    ._15(ram_1_data[5]), .I4(ram_1_data[4]), .I3(ram_1_data[3]), .I2(ram_1_data[2]), .I1(ram_1_data[1]),
    .I0(ram_1_data[0]), .O7(flex_6016_1_o7[7]), .O6(flex_6016_1_o0[6]), .O5(flex_6016_1_o0[5]),
    .O4(flex_6016_1_o0[4]), .O3(flex_6016_1_o0[3]), .O2(flex_6016_1_o0[2]), .O1(flex_6016_1_o0[1]),
    .O0(flex_6016_1_o0[0]), .A0(flex_6016_1_a0[0]), .A1(flex_6016_1_a0[1]), .A2(flex_6016_1_a0[2]),
    .A3(flex_6016_1_a0[3]), .A4(flex_6016_1_a0[4]), .A5(flex_6016_1_a0[5]), .A6(flex_6016_1_a0[6]),
    .A7(flex_6016_1_a0[7]), .A8(flex_6016_1_a0[8]), .A9(flex_6016_1_a0[9]), .A10(flex_6016_1_a0[10]),
    .A11(flex_6016_1_a0[11]), .A12(flex_6016_1_a0[12]), .A13(flex_6016_1_a0[13]), .A14(flex_6016_1_a0[14]),
    .A15(flex_6016_1_a0[15]), .WRITE_MEM(flex_6016_1_write_mem));
  and and_1 (and_1_out, flex_6016_1_a0[0], flex_6016_1_a0[1], flex_6016_1_a0[2], flex_6016_1_a0[3], flex_6016_1_a0[4], flex_6016_1_a0[5], flex_6016_1_a0[6], flex_6016_1_a0[7], flex_6016_1_a0[8], flex_6016_1_a0[9], flex_6016_1_a0[10], flex_6016_1_a0[11], flex_6016_1_a0[12], flex_6016_1_a0[13], flex_6016_1_a0[14], flex_6016_1_a0[15], flex_6016_1_write_mem);
  TTY tty_1 (.data(flex_6016_1_o0), .clk(and_1_out));  // open: we, clr
  RAM #(.addrWidth(16), .bus("separate")) ram_1 (
    .addr(flex_6016_1_a0), .din({flex_6016_1_o7[7], flex_6016_1_o0}), .data(ram_1_data),
    .clk(flex_6016_1_write_mem));  // open: str, sel, ld, clr
endmodule

module RegisterFile (
  input  [15:0] IN,
  input  [7:0] SRC_DEST,
  input  STORE,
  input  [15:0] FLAGS_IN,
  input  [15:0] RA_IN,
  input  STORE_FR,
  input  FR_TO_ALU,
  input  STORE_RA,
  input  ENABLE_RA,
  output [15:0] SRC_OUT,
  output [15:0] DEST_OUT,
  output [15:0] RA_OUT,
  output [7:0] FLAG_OUT
);

  wire and_1_out, and_2_out, and_3_out, and_4_out, and_5_out, and_6_out, and_7_out, and_8_out, and_9_out,
       and_10_out, and_11_out, and_12_out, and_13_out, and_14_out, and_15_out, decoder_1_out0,
       decoder_1_out1, decoder_1_out2, decoder_1_out3, decoder_2_out0, decoder_2_out1, decoder_2_out2,
       decoder_2_out3, duelreg_1_enable, duelreg_1_trigger, duelreg_2_enable, duelreg_2_trigger;
  wire [15:0] duelreg_1_data, duelreg_2_data, register_1_q, register_2_q, register_3_q, register_4_q,
       register_5_q, register_6_q, register_8_q, register_9_q, register_10_q, register_11_q, register_12_q,
       register_13_q, register_14_q;
  wire [15:8] register_15_q;

  Decoder #(.select(2)) decoder_1 (
    .out0(decoder_1_out0), .out1(decoder_1_out1), .out2(decoder_1_out2), .out3(decoder_1_out3),
    .sel(SRC_DEST[1:0]));  // open: en
  Decoder #(.select(2)) decoder_2 (
    .out0(decoder_2_out0), .out1(decoder_2_out1), .out2(decoder_2_out2), .out3(decoder_2_out3),
    .sel(SRC_DEST[3:2]));  // open: en
  and and_1 (and_1_out, decoder_1_out0, decoder_2_out1);
  and and_2 (and_2_out, decoder_1_out0, decoder_2_out2);
  and and_3 (and_3_out, decoder_1_out0, decoder_2_out3);
  Register #(.width(16)) register_1 (.D(IN), .en(and_1_out), .Q(register_1_q), .clk(STORE));  // open: clr
  Register #(.width(16)) register_2 (.D(IN), .en(and_2_out), .Q(register_2_q), .clk(STORE));  // open: clr
  Register #(.width(16)) register_3 (.D(IN), .en(and_3_out), .Q(register_3_q), .clk(STORE));  // open: clr
  and and_4 (and_4_out, decoder_1_out1, decoder_2_out0);
  and and_5 (and_5_out, decoder_1_out1, decoder_2_out1);
  and and_6 (and_6_out, decoder_1_out1, decoder_2_out2);
  and and_7 (and_7_out, decoder_2_out3, decoder_1_out1);
  DUELREG duelreg_1 (
    .INPUT_A(IN), .INPUT_B(RA_IN), .EnableA(and_7_out), .Enable_B(ENABLE_RA), .TrigerA(STORE),
    .TrigerB(STORE_RA), .USE_B(ENABLE_RA), .Data(duelreg_1_data), .Enable(duelreg_1_enable),
    .Trigger(duelreg_1_trigger));
  Register #(.width(16)) register_4 (.D(IN), .en(and_4_out), .Q(register_4_q), .clk(STORE));  // open: clr
  Register #(.width(16)) register_5 (.D(IN), .en(and_5_out), .Q(register_5_q), .clk(STORE));  // open: clr
  Register #(.width(16)) register_6 (.D(IN), .en(and_6_out), .Q(register_6_q), .clk(STORE));  // open: clr
  Register #(.width(16)) register_7 (
    .D(duelreg_1_data), .en(duelreg_1_enable), .Q(RA_OUT), .clk(duelreg_1_trigger));  // open: clr
  Register #(.width(16)) register_8 (.D(IN), .en(and_8_out), .Q(register_8_q), .clk(STORE));  // open: clr
  and and_8 (and_8_out, decoder_1_out2, decoder_2_out0);
  Register #(.width(16)) register_9 (.D(IN), .en(and_9_out), .Q(register_9_q), .clk(STORE));  // open: clr
  and and_9 (and_9_out, decoder_1_out2, decoder_2_out1);
  Register #(.width(16)) register_10 (.D(IN), .en(and_10_out), .Q(register_10_q), .clk(STORE));  // open: clr
  and and_10 (and_10_out, decoder_1_out2, decoder_2_out2);
  Register #(.width(16)) register_11 (.D(IN), .en(and_11_out), .Q(register_11_q), .clk(STORE));  // open: clr
  and and_11 (and_11_out, decoder_1_out2, decoder_2_out3);
  and and_12 (and_12_out, decoder_1_out3, decoder_2_out0);
  and and_13 (and_13_out, decoder_1_out3, decoder_2_out1);
  and and_14 (and_14_out, decoder_1_out3, decoder_2_out2);
  and and_15 (and_15_out, decoder_2_out3, decoder_1_out3);
  Register #(.width(16)) register_12 (.D(IN), .en(and_12_out), .Q(register_12_q), .clk(STORE));  // open: clr
  Register #(.width(16)) register_13 (.D(IN), .en(and_13_out), .Q(register_13_q), .clk(STORE));  // open: clr
  Register #(.width(16)) register_14 (.D(IN), .en(and_14_out), .Q(register_14_q), .clk(STORE));  // open: clr
  DUELREG duelreg_2 (
    .INPUT_A(IN), .INPUT_B(FLAGS_IN), .EnableA(FR_TO_ALU), .Enable_B(and_15_out), .TrigerA(STORE),
    .TrigerB(STORE_FR), .USE_B(FR_TO_ALU), .Data(duelreg_2_data), .Enable(duelreg_2_enable),
    .Trigger(duelreg_2_trigger));
  Register #(.width(16)) register_15 (
    .D(duelreg_2_data), .en(duelreg_2_enable), .Q({register_15_q, FLAG_OUT}), .clk(duelreg_2_trigger));  // open: clr
  Multiplexer #(.select(4), .width(16)) multiplexer_1 (
    .in0({16{1'b0}}), .in1(register_4_q), .in2(register_8_q), .in3(register_12_q), .in4(register_1_q),
    .in5(register_5_q), .in6(register_9_q), .in7(register_13_q), .in8(register_2_q), .in9(register_6_q),
    .in10(register_10_q), .in11(register_14_q), .in12(register_3_q), .in13(RA_OUT), .in14(register_11_q),
    .in15({register_15_q, FLAG_OUT}), .out(SRC_OUT), .sel(SRC_DEST[7:4]));  // open: en
  Multiplexer #(.select(4), .width(16)) multiplexer_2 (
    .in0({16{1'b0}}), .in1(register_4_q), .in2(register_8_q), .in3(register_12_q), .in4(register_1_q),
    .in5(register_5_q), .in6(register_9_q), .in7(register_13_q), .in8(register_2_q), .in9(register_6_q),
    .in10(register_10_q), .in11(register_14_q), .in12(register_3_q), .in13(RA_OUT), .in14(register_11_q),
    .in15({register_15_q, FLAG_OUT}), .out(DEST_OUT), .sel(SRC_DEST[3:0]));  // open: en
  Clock clock_1 ();  // open: out
endmodule

module DUELREG (
  input  [15:0] INPUT_A,
  input  [15:0] INPUT_B,
  input  EnableA,
  input  Enable_B,
  input  USE_B,
  input  TrigerA,
  input  TrigerB,
  output [15:0] Data,
  output Enable,
  output Trigger
);

  or or_1 (Enable, EnableA, Enable_B);
  Multiplexer #(.width(16)) multiplexer_1 (.in0(INPUT_A), .in1(INPUT_B), .out(Data), .sel(USE_B));  // open: en
  or or_2 (Trigger, TrigerA, TrigerB);
endmodule

module ADDRESS_PLEXER (
  input  [15:0] PC_IN,
  input  [15:0] SRC_IN,
  input  [15:0] DEST_IN,
  input  [15:0] IM_IN,
  input  [2:0] OFFSET,
  input  SRC,
  input  DEST,
  input  NMI,
  input  IRQ,
  input  USE_IM_OFFSET,
  output [15:0] ADDR_OUT
);

  wire and_1_out, or_1_out, or_2_out;
  wire [15:0] add_sub_1_value, bit_extender_1_out, multiplexer_1_out, multiplexer_2_out, multiplexer_3_out,
       multiplexer_4_out, multiplexer_5_out, multiplexer_6_out;

  Multiplexer #(.width(16)) multiplexer_1 (
    .in0(SRC_IN), .in1(DEST_IN), .out(multiplexer_1_out), .sel(DEST));  // open: en
  Multiplexer #(.width(16)) multiplexer_2 (
    .in0({16{1'b0}}), .in1(16'h2), .out(multiplexer_2_out), .sel(IRQ));  // open: en
  Multiplexer #(.width(16)) multiplexer_3 (
    .in0(multiplexer_1_out), .in1(multiplexer_2_out), .out(multiplexer_3_out), .sel(or_2_out));  // open: en
  and and_1 (and_1_out, SRC, DEST);
  Multiplexer #(.width(16)) multiplexer_4 (
    .in0(PC_IN), .in1(multiplexer_3_out), .out(multiplexer_4_out), .sel(or_1_out));  // open: en
  or or_1 (or_1_out, SRC, DEST, or_2_out);
  or or_2 (or_2_out, NMI, IRQ);
  Multiplexer #(.width(16)) multiplexer_5 (
    .in0(multiplexer_4_out), .in1(IM_IN), .out(multiplexer_5_out), .sel(and_1_out));  // open: en
  Multiplexer #(.width(16)) multiplexer_6 (
    .in0({16{1'b0}}), .in1(IM_IN), .out(multiplexer_6_out), .sel(USE_IM_OFFSET));  // open: en
  ADD_SUB add_sub_1 (.BASE(multiplexer_5_out), .SIGNED(multiplexer_6_out), .VALUE(add_sub_1_value));
  Adder #(.width(16)) adder_1 (.a(add_sub_1_value), .b(bit_extender_1_out), .out(ADDR_OUT));  // open: cin, cout
  assign bit_extender_1_out = {{13{1'b0}}, OFFSET};  // Bit_Extender bit_extender_1
endmodule

module ADD_SUB (
  input  [15:0] BASE,
  input  [15:0] SIGNED,
  output [15:0] VALUE
);

  wire [15:0] adder_1_out, subtractor_1_out;

  Adder #(.width(16)) adder_1 (.a(BASE), .b({1'b0, SIGNED[14:0]}), .out(adder_1_out));  // open: cin, cout
  Multiplexer #(.width(16)) multiplexer_1 (
    .in0(adder_1_out), .in1(subtractor_1_out), .out(VALUE), .sel(SIGNED[15]));  // open: en
  Subtractor #(.width(16)) subtractor_1 (
    .a(BASE), .b({1'b0, SIGNED[14:0]}), .out(subtractor_1_out));  // open: bin, bout
endmodule

module PC_SELECT (
  input  [7:0] FLAGS,
  input  [7:0] INS,
  input  [15:0] ADDR_IN,
  input  [15:0] PC_IN,
  input  [15:0] SRC,
  input  [15:0] RA,
  input  [15:0] IR_RA,
  input  [15:0] MEMORY,
  input  PC_BRANCH,
  input  PC_SRC,
  input  PC_RA,
  input  PC_IR_RA,
  output [15:0] PC_OUT
);

  wire and_1_out, multiplexer_2_out, not_1_out, or_1_out;
  wire [1:0] or_3_out;
  wire [15:0] add_sub_1_value, multiplexer_1_out;

  Multiplexer #(.width(16)) multiplexer_1 (.in0(SRC), .in1(RA), .out(multiplexer_1_out), .sel(PC_RA));  // open: en
  ADD_SUB add_sub_1 (.BASE(PC_IN), .SIGNED(MEMORY), .VALUE(add_sub_1_value));
  not not_1 (not_1_out, FLAGS[3]);
  Multiplexer #(.select(3)) multiplexer_2 (
    .in0(FLAGS[0]), .in1(FLAGS[1]), .in2(FLAGS[2]), .in3(FLAGS[3]), .in4(FLAGS[4]), .in5(not_1_out),
    .in6(1'b1), .in7(FLAGS[7]), .out(multiplexer_2_out), .sel(INS[2:0]));  // open: en
  and and_1 (and_1_out, multiplexer_2_out, PC_BRANCH);
  or or_1 (or_1_out, PC_SRC, PC_RA);
  Multiplexer #(.select(2), .width(16)) multiplexer_3 (
    .in0(ADDR_IN), .in1(add_sub_1_value), .in2(multiplexer_1_out), .in3(IR_RA), .out(PC_OUT), .sel(or_3_out));  // open: en
  or or_2 (or_3_out[1], or_1_out, PC_IR_RA);
  or or_3 (or_3_out[0], and_1_out, PC_IR_RA);
endmodule

module DATA_INPUT (
  input  [7:0] Raw_DATA,
  input  [7:0] BYTE_REG,
  input  ZERO_EXTENDED,
  input  SIGNED_EXTENDED,
  input  NEGITIVE_EXTENDED,
  output [15:0] FULL_OUT,
  output [7:0] RAW_OUT
);

  wire or_1_out, or_2_out;
  wire [15:0] bit_extender_1_out, bit_extender_2_out, multiplexer_1_out, multiplexer_2_out;

  assign bit_extender_1_out = {{8{1'b0}}, Raw_DATA};  // Bit_Extender bit_extender_1
  assign bit_extender_2_out = {{8{Raw_DATA[7]}}, Raw_DATA};  // Bit_Extender bit_extender_2
  Multiplexer #(.width(16)) multiplexer_1 (
    .in0({Raw_DATA[7], {8{1'b0}}, Raw_DATA[6:0]}), .in1(bit_extender_2_out), .out(multiplexer_1_out),
    .sel(NEGITIVE_EXTENDED));  // open: en
  Multiplexer #(.width(16)) multiplexer_2 (
    .in0(bit_extender_1_out), .in1(multiplexer_1_out), .out(multiplexer_2_out), .sel(or_2_out));  // open: en
  or or_1 (or_1_out, ZERO_EXTENDED, or_2_out);
  or or_2 (or_2_out, SIGNED_EXTENDED, NEGITIVE_EXTENDED);
  Multiplexer #(.width(16)) multiplexer_3 (
    .in0({BYTE_REG, Raw_DATA}), .in1(multiplexer_2_out), .out(FULL_OUT), .sel(or_1_out));  // open: en

  assign RAW_OUT = Raw_DATA;
endmodule

module ALU (
  input  [7:0] INS,
  input  [7:0] FLAGS,
  input  [15:0] SRC,
  input  [15:0] DEST,
  input  [15:0] MEMORY,
  input  USE_MEMORY,
  input  UNSIGNED_COMP,
  input  SIGMED_COMP,
  output [15:0] ANS,
  output [15:0] FLAGS_2
);

  wire adder_1_cout, or_2_out, subtractor_1_bout;
  wire [0:0] and_1_out;
  wire [1:0] comparator_3_eq;
  wire [3:0] bit_extender_1_out, bit_extender_2_out;
  wire [4:2] comparator_1_lt, comparator_2_lt;
  wire [7:0] multiplexer_2_out, multiplexer_5_out;
  wire [15:0] adder_1_out, and_2_out, multiplexer_1_out, negator_1_out, or_1_out, shifter_1_out,
       shifter_2_out, subtractor_1_out, xor_1_out;

  Multiplexer #(.width(16)) multiplexer_1 (
    .in0(DEST), .in1(MEMORY), .out(multiplexer_1_out), .sel(USE_MEMORY));  // open: en
  and and_1 (and_1_out[0], FLAGS[0], INS[0]);
  Bit_Extender #(.in_width(16), .out_width(4)) bit_extender_1 (.in(multiplexer_1_out), .out(bit_extender_1_out));
  Bit_Extender #(.in_width(16), .out_width(4)) bit_extender_2 (.in(multiplexer_1_out), .out(bit_extender_2_out));
  Comparator #(.width(16), .mode("unsigned")) comparator_1 (
    .a(SRC), .b(multiplexer_1_out), .gt(comparator_1_lt[4]), .eq(comparator_1_lt[3]), .lt(comparator_1_lt[2]));
  Comparator #(.width(16), .mode("unsigned")) comparator_2 (
    .a(SRC), .b(multiplexer_1_out), .gt(comparator_2_lt[4]), .eq(comparator_2_lt[3]), .lt(comparator_2_lt[2]));
  Adder #(.width(16)) adder_1 (
    .a(SRC), .b(multiplexer_1_out), .out(adder_1_out), .cin(and_1_out[0]), .cout(adder_1_cout));
  Subtractor #(.width(16)) subtractor_1 (
    .a(SRC), .b(multiplexer_1_out), .out(subtractor_1_out), .bin(and_1_out[0]), .bout(subtractor_1_bout));
  assign and_2_out = SRC & multiplexer_1_out;  // AND_Gate and_2, 16 bits wide
  assign or_1_out = SRC | multiplexer_1_out;  // OR_Gate or_1, 16 bits wide
  assign xor_1_out = SRC ^ multiplexer_1_out;  // XOR_Gate xor_1, 16 bits wide
  Negator #(.width(16)) negator_1 (.in(multiplexer_1_out), .out(negator_1_out));
  Shifter #(.width(16)) shifter_1 (.in(SRC), .\dist (bit_extender_1_out), .out(shifter_1_out));
  Shifter #(.width(16), .shift("lr")) shifter_2 (.in(SRC), .\dist (bit_extender_2_out), .out(shifter_2_out));
  Multiplexer #(.width(8)) multiplexer_2 (
    .in0({FLAGS[7], 2'b00, comparator_1_lt, 2'b00}), .in1({FLAGS[7], 2'b00, comparator_2_lt, 2'b00}),
    .out(multiplexer_2_out), .sel(SIGMED_COMP));  // open: en
  or or_2 (or_2_out, UNSIGNED_COMP, SIGMED_COMP);
  Multiplexer #(.select(3), .width(16)) multiplexer_3 (
    .in0(adder_1_out), .in1(subtractor_1_out), .in2(and_2_out), .in3(or_1_out), .in4(xor_1_out),
    .in5(negator_1_out), .in6({shifter_1_out[15:1], and_1_out[0]}),
    .in7({and_1_out[0], shifter_2_out[14:0]}), .out(ANS), .sel(INS[3:1]));  // open: en
  Multiplexer #(.select(3)) multiplexer_4 (
    .in0(adder_1_cout), .in1(subtractor_1_bout), .in2(1'b0), .in3(1'b0), .in4(1'b0), .in5(1'b0),
    .in6(SRC[15]), .in7(SRC[0]), .out(comparator_3_eq[1]), .sel(INS[3:1]));  // open: en
  Comparator #(.width(16), .mode("unsigned")) comparator_3 (
    .a(ANS), .b({16{1'b0}}), .eq(comparator_3_eq[0]));  // open: gt, lt
  Multiplexer #(.width(8)) multiplexer_5 (
    .in0({FLAGS[7], {5{1'b0}}, comparator_3_eq}), .in1(multiplexer_2_out), .out(multiplexer_5_out),
    .sel(or_2_out));  // open: en
  assign FLAGS_2 = {{8{1'b0}}, multiplexer_5_out};  // Bit_Extender bit_extender_3
  // AND_Gate and_3 is placed but not wired
endmodule

module FLEX_6016 (
  input  I7,
  input  I6,
  input  _15,
  input  I4,
  input  I3,
  input  I2,
  input  I1,
  input  I0,
  input  IRQ,
  input  NMI,
  input  CLOCK,
  output A0,
  output A1,
  output A2,
  output A3,
  output A4,
  output A5,
  output A6,
  output A7,
  output A8,
  output A9,
  output A10,
  output A11,
  output A12,
  output A13,
  output A14,
  output A15,
  output WRITE_MEM,
  output O7,
  output O6,
  output O5,
  output O4,
  output O3,
  output O2,
  output O1,
  output O0
);

  wire ADDR_DEST, ADDR_IRQ, ADDR_NMI, ADDR_SRC, CMP, DEST_ADDR, DEST_ALU, DEST_SRC, FR_ALU, NEG_EXTEND,
       OUT_HIGH, PC_BRANCH, PC_IRQ_RA, PC_RA, PC_SRC, RA_ADDR, SCMP, SIGNED_EXTEND, STORE_BYTE, STORE_DEST,
       STORE_FR, STORE_IM, STORE_INS, STORE_IRQ_RA, STORE_PC, STORE_RA, STORE_SRC_DEST, USE_IM_OFFSET,
       USE_MEM, ZERO_EXTEND;
  wire [2:0] ADDR_OFFSET;
  wire [7:0] BYTE_REG_q, data_input_1_raw_out, INS_q, registerfile_1_flag_out, SRC_DEST_q;
  wire [15:0] alu_1_ans, alu_1_flags_2, data_input_1_full_out, dest_select_1_to_dest, IM_q, PC_q,
       pc_select_1_pc_out, register_1_q, registerfile_1_dest_out, registerfile_1_ra_out,
       registerfile_1_src_out;

  Register BYTE_REG (.D({I7, I6, _15, I4, I3, I2, I1, I0}), .Q(BYTE_REG_q), .clk(STORE_BYTE));  // open: en, clr
  DATA_INPUT data_input_1 (
    .Raw_DATA({I7, I6, _15, I4, I3, I2, I1, I0}), .BYTE_REG(BYTE_REG_q), .ZERO_EXTENDED(ZERO_EXTEND),
    .SIGNED_EXTENDED(SIGNED_EXTEND), .NEGITIVE_EXTENDED(NEG_EXTEND), .FULL_OUT(data_input_1_full_out),
    .RAW_OUT(data_input_1_raw_out));
  DATA_OUT data_out_1 (.out_3({O7, O6, O5, O4, O3, O2, O1, O0}), .OUT_HIGH(OUT_HIGH), .SRC(registerfile_1_src_out));
  CONTROL_UNIT control_unit_1 (
    .IRQ(IRQ), .NMI(NMI), .CLOCK(CLOCK), .ZERO_EXTEND(ZERO_EXTEND), .SIGN_EXTEND(SIGNED_EXTEND),
    .NEG_EXTEND(NEG_EXTEND), .DEST_ALU(DEST_ALU), .DEST_SRC(DEST_SRC), .DEST_ADDR(DEST_ADDR),
    .PC_BRANCH(PC_BRANCH), .PC_SRC(PC_SRC), .PC_RA(PC_RA), .PC_IRQ_RA(PC_IRQ_RA), .ALU_TO_FR(FR_ALU),
    .ADDR_TO_RA(RA_ADDR), .ALU_USE_MEMORY(USE_MEM), .CMP(CMP), .SCMP(SCMP), .ADR_SRC(ADDR_SRC),
    .ADR_DEST(ADDR_DEST), .ADR_IRQ(ADDR_IRQ), .ADR_NMI(ADDR_NMI), .USE_IM_OFFSET(USE_IM_OFFSET),
    .STORE_FR(STORE_FR), .STORE_RA(STORE_RA), .STORE_DEST(STORE_DEST), .STORE_PC(STORE_PC),
    .STORE_BYTE(STORE_BYTE), .STORE_INS(STORE_INS), .STORE_SRC_DEST(STORE_SRC_DEST),
    .STORE_IRQ_RA(STORE_IRQ_RA), .STORE_IM(STORE_IM), .WRITE_MEM(WRITE_MEM), .OFFSET(ADDR_OFFSET),
    .INS(INS_q), .FLAGS(registerfile_1_flag_out), .OUT_HIGH(OUT_HIGH));
  Register INS (.D(data_input_1_raw_out), .Q(INS_q), .clk(STORE_INS));  // open: en, clr
  Register SRC_DEST (.D(data_input_1_raw_out), .Q(SRC_DEST_q), .clk(STORE_SRC_DEST));  // open: en, clr
  ALU alu_1 (
    .SRC(registerfile_1_src_out), .DEST(registerfile_1_dest_out), .MEMORY(data_input_1_full_out),
    .USE_MEMORY(USE_MEM), .INS(INS_q), .FLAGS(registerfile_1_flag_out), .UNSIGNED_COMP(CMP),
    .SIGMED_COMP(SCMP), .ANS(alu_1_ans), .FLAGS_2(alu_1_flags_2));
  Register #(.width(16)) IM (.D(data_input_1_full_out), .Q(IM_q), .clk(STORE_IM));  // open: en, clr
  Register #(.width(16)) register_1 (.D(PC_q), .Q(register_1_q), .clk(STORE_IRQ_RA));  // open: en, clr
  PC_SELECT pc_select_1 (
    .ADDR_IN({A15, A14, A13, A12, A11, A10, A9, A8, A7, A6, A5, A4, A3, A2, A1, A0}),
    .SRC(registerfile_1_src_out), .RA(registerfile_1_ra_out), .IR_RA(register_1_q), .MEMORY(IM_q),
    .INS(INS_q), .FLAGS(registerfile_1_flag_out), .PC_BRANCH(PC_BRANCH), .PC_SRC(PC_SRC), .PC_RA(PC_RA),
    .PC_IR_RA(PC_IRQ_RA), .PC_OUT(pc_select_1_pc_out), .PC_IN(PC_q));
  DEST_SELECT dest_select_1 (
    .MEMORY(data_input_1_full_out), .ALU(alu_1_ans), .SRC(registerfile_1_src_out),
    .ADDR({A15, A14, A13, A12, A11, A10, A9, A8, A7, A6, A5, A4, A3, A2, A1, A0}), .ADDR_2(DEST_ADDR),
    .SRC_2(DEST_SRC), .ALU_2(DEST_ALU), .TO_DEST(dest_select_1_to_dest));
  ADDRESS_PLEXER address_plexer_1 (
    .PC_IN(PC_q), .SRC_IN(registerfile_1_src_out), .DEST_IN(registerfile_1_dest_out), .IM_IN(IM_q),
    .SRC(ADDR_SRC), .DEST(ADDR_DEST), .NMI(ADDR_NMI), .IRQ(ADDR_IRQ), .USE_IM_OFFSET(USE_IM_OFFSET),
    .OFFSET(ADDR_OFFSET), .ADDR_OUT({A15, A14, A13, A12, A11, A10, A9, A8, A7, A6, A5, A4, A3, A2, A1, A0}));
  RegisterFile registerfile_1 (
    .IN(dest_select_1_to_dest), .SRC_DEST(SRC_DEST_q), .STORE(STORE_DEST), .STORE_FR(STORE_FR),
    .FR_TO_ALU(FR_ALU), .FLAGS_IN(alu_1_flags_2), .FLAG_OUT(registerfile_1_flag_out), .STORE_RA(STORE_RA),
    .ENABLE_RA(RA_ADDR), .RA_IN({A15, A14, A13, A12, A11, A10, A9, A8, A7, A6, A5, A4, A3, A2, A1, A0}),
    .RA_OUT(registerfile_1_ra_out), .SRC_OUT(registerfile_1_src_out), .DEST_OUT(registerfile_1_dest_out));
  Register #(.width(16)) PC (.D(pc_select_1_pc_out), .Q(PC_q), .clk(STORE_PC));  // open: en, clr
  D_Flip_Flop d_ff_1 ();  // open: clk, D, Q, Qn, preset, en, reset
endmodule

module DATA_OUT (
  input  [15:0] SRC,
  input  OUT_HIGH,
  output [7:0] out_3
);

  Multiplexer #(.width(8)) multiplexer_1 (.in0(SRC[7:0]), .in1(SRC[15:8]), .out(out_3), .sel(OUT_HIGH));  // open: en
endmodule

module DEST_SELECT (
  input  [15:0] MEMORY,
  input  [15:0] ALU,
  input  [15:0] SRC,
  input  [15:0] ADDR,
  input  ADDR_2,
  input  SRC_2,
  input  ALU_2,
  output [15:0] TO_DEST
);

  wire or_1_out;
  wire [15:0] multiplexer_1_out, multiplexer_2_out;

  Multiplexer #(.width(16)) multiplexer_1 (.in0(MEMORY), .in1(ALU), .out(multiplexer_1_out), .sel(ALU_2));  // open: en
  Multiplexer #(.width(16)) multiplexer_2 (.in0(SRC), .in1(ADDR), .out(multiplexer_2_out), .sel(ADDR_2));  // open: en
  Multiplexer #(.width(16)) multiplexer_3 (
    .in0(multiplexer_1_out), .in1(multiplexer_2_out), .out(TO_DEST), .sel(or_1_out));  // open: en
  or or_1 (or_1_out, ADDR_2, SRC_2);
endmodule

module CONTROL_UNIT (
  input  [7:0] INS,
  input  [7:0] FLAGS,
  input  IRQ,
  input  NMI,
  input  CLOCK,
  output ZERO_EXTEND,
  output SIGN_EXTEND,
  output NEG_EXTEND,
  output DEST_ALU,
  output DEST_SRC,
  output DEST_ADDR,
  output PC_BRANCH,
  output PC_SRC,
  output PC_RA,
  output PC_IRQ_RA,
  output ALU_TO_FR,
  output ADDR_TO_RA,
  output ALU_USE_MEMORY,
  output CMP,
  output SCMP,
  output ADR_SRC,
  output ADR_DEST,
  output ADR_IRQ,
  output ADR_NMI,
  output USE_IM_OFFSET,
  output OUT_HIGH,
  output STORE_FR,
  output STORE_RA,
  output STORE_DEST,
  output STORE_PC,
  output STORE_BYTE,
  output STORE_INS,
  output STORE_SRC_DEST,
  output STORE_IRQ_RA,
  output STORE_IM,
  output WRITE_MEM,
  output [2:0] OFFSET
);

  wire and_1_out, and_2_out, and_3_out, and_4_out, and_5_out, and_6_out, and_7_out, and_8_out, and_9_out,
       and_10_out, and_11_out, comparator_1_eq, d_ff_1_q, d_ff_1_qn, d_ff_2_qn, d_ff_3_q, d_ff_3_qn,
       d_ff_4_qn, decoder_3_out0, not_1_out, not_2_out, or_1_out, or_2_out, or_3_out, or_4_out, or_5_out;
  wire [1:0] rom_2_data_3, rom_2_data_4, rom_2_data_5;
  wire [7:0] counter_1_q, rom_1_data;
  wire [8:0] bit_extender_1_out, multiplexer_1_out, multiplexer_2_out;
  wire [9:2] rom_2_data_2;
  wire [31:2] rom_2_data;

  Multiplexer #(.width(9)) multiplexer_1 (
    .in0(bit_extender_1_out), .in1(multiplexer_2_out), .out(multiplexer_1_out), .sel(and_9_out));  // open: en
  Comparator #(.width(9), .mode("unsigned")) comparator_1 (
    .a(bit_extender_1_out), .b(9'hff), .eq(comparator_1_eq));  // open: gt, lt
  and and_1 (and_1_out, d_ff_2_qn, rom_2_data[27]);
  and and_2 (and_2_out, ~d_ff_2_qn, rom_2_data[28]);  // AND_Gate
  and and_3 (and_3_out, d_ff_1_qn, or_5_out);
  and and_4 (and_4_out, ~d_ff_1_qn, rom_2_data[30]);  // AND_Gate
  and and_5 (and_5_out, not_1_out, IRQ);
  and and_6 (and_6_out, d_ff_3_qn, NMI);
  and and_7 (and_7_out, ~d_ff_3_qn, rom_2_data[30]);  // AND_Gate
  assign bit_extender_1_out = {{1{1'b0}}, INS};  // Bit_Extender bit_extender_1
  Multiplexer #(.width(9)) multiplexer_2 (
    .in0(9'h100), .in1(9'h101), .out(multiplexer_2_out), .sel(d_ff_3_q));  // open: en
  or or_1 (or_1_out, and_2_out, and_1_out);
  or or_2 (or_2_out, and_4_out, and_3_out);
  D_Flip_Flop d_ff_1 (.clk(or_2_out), .D(d_ff_1_qn), .Q(d_ff_1_q), .Qn(d_ff_1_qn));  // open: preset, en, reset
  or or_3 (or_3_out, and_5_out, and_8_out);
  and and_8 (and_8_out, not_1_out, rom_2_data[29]);
  or or_4 (or_4_out, and_7_out, and_6_out);
  ROM #(.addrWidth(9)) rom_1 (.addr(multiplexer_1_out), .data(rom_1_data));  // open: sel
  D_Flip_Flop d_ff_2 (.clk(or_1_out), .D(d_ff_2_qn), .Qn(d_ff_2_qn));  // open: Q, preset, en, reset
  or or_5 (or_5_out, or_3_out, d_ff_3_q);
  D_Flip_Flop d_ff_3 (.clk(or_4_out), .D(d_ff_3_qn), .Q(d_ff_3_q), .Qn(d_ff_3_qn));  // open: preset, en, reset
  not not_1 (not_1_out, FLAGS[7]);
  and and_9 (and_9_out, d_ff_2_qn, d_ff_1_q);
  Counter counter_1 (
    .load(rom_2_data[31]), .D(rom_1_data), .count(not_2_out), .Q(counter_1_q), .clk(and_10_out));  // open: carry, clr
  not not_2 (not_2_out, rom_2_data[31]);
  and and_10 (and_10_out, CLOCK, d_ff_4_qn);
  and and_11 (and_11_out, comparator_1_eq, rom_2_data[31]);
  D_Flip_Flop d_ff_4 (.clk(and_11_out), .D(d_ff_4_qn), .Qn(d_ff_4_qn));  // open: Q, preset, en, reset
  ROM #(.dataWidth(32)) rom_2 (
    .addr(counter_1_q),
    .data({rom_2_data[31:27], OFFSET, rom_2_data_2, USE_IM_OFFSET, rom_2_data_5, ADR_SRC, OUT_HIGH, CMP, ALU_USE_MEMORY, ADDR_TO_RA, ALU_TO_FR, rom_2_data_3, rom_2_data[4:2], rom_2_data_4}));  // open: sel
  Multiplexer #(.width(10)) multiplexer_3 (
    .in0({rom_2_data_2, ADDR_TO_RA, ALU_TO_FR}), .in1({10{1'b0}}),
    .out({WRITE_MEM, STORE_IM, STORE_IRQ_RA, STORE_SRC_DEST, STORE_INS, STORE_BYTE, STORE_PC, STORE_DEST, STORE_RA, STORE_FR}),
    .sel(CLOCK));  // open: en
  Decoder #(.select(2)) decoder_1 (
    .out1(ZERO_EXTEND), .out2(SIGN_EXTEND), .out3(NEG_EXTEND), .sel(rom_2_data_4));  // open: out0, en
  Decoder #(.select(2)) decoder_2 (
    .out1(DEST_ALU), .out2(DEST_SRC), .out3(DEST_ADDR), .sel(rom_2_data[3:2]));  // open: out0, en
  Decoder #(.select(2)) decoder_3 (
    .out0(decoder_3_out0), .out1(PC_SRC), .out2(PC_RA), .out3(PC_IRQ_RA), .sel(rom_2_data_3));  // open: en
  and and_12 (PC_BRANCH, rom_2_data[4], decoder_3_out0);
  Decoder #(.select(2)) decoder_4 (
    .out1(ADR_DEST), .out2(ADR_IRQ), .out3(ADR_NMI), .sel(rom_2_data_5));  // open: out0, en
  Bit_Extender bit_extender_2 ();  // open: in, out

  assign SCMP = OUT_HIGH;

  // Notes on the sheet:
  //   contents of rom_1 (hex, n*v repeats v):
  //   16*0 3 7 0 0 c 11 0 0 17 1d 6*0 24 28 0 0 2d 32 0 0 38 3e 6*0 45 28 0 0 49 32 0 0 4e 3e 6*0 5*54 0
  //   54 0 54 0 54 0 4*54 5*57 0 57 0 57 0 57 0 4*57 5*5b 0 5b 0 5b 7*0 60 63 14*0 8*66 7*0 6a 6*0 6d 8*0
  //   72 76 16*0 87 13*0 7e 78 63*0 82 88
  //   contents of rom_2 (hex, n*v repeats v):
  //   0 1020000 80080000 1100000 802000 2020000 80080000 1100000 802800 1802000 2020000 80080000 1100000
  //   2400002 80a000 3020000 80080000 1100000 2400002 80a800 180a000 3020000 80080000 1100000 2040000
  //   3400000 809000 4020000 80080000 1100000 2040000 3400000 80a800 180a000 4020000 80080000 1100000
  //   11001 2020000 80080000 1100000 41000 1011000 2020000 80080000 1100000 2400002 19001 3020000 80080000
  //   1100000 2400002 49000 1019000 3020000 80080000 1100000 2040000 3400000 19001 4020000 80080000
  //   1100000 2040000 3400000 49000 1019000 4020000 80080000 1100000 11003 2020000 80080000 1100000
  //   2400002 19003 3020000 80080000 1100000 2040000 3400000 19003 4020000 80080000 1100000 2030084
  //   80080000 1100000 2010285 3020000 80080000 1100000 2040000 3010284 4020000 80080000 1100000 2020480
  //   80080000 1100000 2020480 80080000 1040000 2400000 3020010 80080000 1100000 20020 80080000 3000100
  //   1040000 2400000 3020010 80080000 2000100 1100000 20020 80080000 20040 80080000 1100000 2040000
  //   3400000 1800c 4020000 80080000 10020060 80080000 1020000 a0080000 200000 48044000 1404000 23000
  //   80080000 1020000 200000 48046000 1406000 23000 80080000
endmodule
